# Fritzing sketch 1015_5 (saved by Fritzing 1.0.3b)
breadboards: 2

parts:
  R1 = Resistor [tolerance=±5% power=0.25W resistance=1k package=THT]
  LED1 = smd LED [color="Red (633nm)" package="0603 [SMD]"]
  Raspberry_Pi_Pico_W = Raspberry Pi Pico W
  Arduino_UNO = Arduino Uno (Rev3) - ICSP
  R4 = Resistor [tolerance=±5% power=0.25W resistance=1k package=THT]
  LED3 = smd LED [color="Red (633nm)" package="0603 [SMD]"]
  LED2 = smd LED [color="Red (633nm)" package="0603 [SMD]"]
  R2 = Resistor [tolerance=±5% power=0.25W resistance=1k package=THT]
  LED4 = smd LED [color="Red (633nm)" package="0603 [SMD]"]
  R3 = Resistor [tolerance=±5% power=0.25W resistance=1k package=THT]

nets:
  N1: R1.Pin_0, Raspberry_Pi_Pico_W.pin_20
  N2: R1.Pin_1, LED1.anode
  RPi GND: LED1.cathode, Raspberry_Pi_Pico_W.pin_3, Raspberry_Pi_Pico_W.pin_8, Raspberry_Pi_Pico_W.pin_13, Raspberry_Pi_Pico_W.pin_18, Raspberry_Pi_Pico_W.pin_23, Raspberry_Pi_Pico_W.pin_28, Raspberry_Pi_Pico_W.pin_33, Raspberry_Pi_Pico_W.pin_38, LED2.cathode
  N3: Raspberry_Pi_Pico_W.pin_21, R2.Pin_0
  N4: Arduino_UNO.D9_PWM, R4.Pin_1
  N5: Arduino_UNO.D10_PWM/SS, R3.Pin_1
  Arduino GND: Arduino_UNO.GND, LED3.cathode, LED4.cathode
  N6: R4.Pin_0, LED3.anode
  N7: LED2.anode, R2.Pin_1
  N8: LED4.anode, R3.Pin_0

custom parts:
  Raspberry Pi Pico W: Raspberry Pi Pico W. Based around the RP2040 microcontroller the Pico W is a low cost microcontroller device bringing Raspberry Pi quality, cost, and easy of use to the microcontroller space. The areas marked KEEPOUT in pcb silkscreen should not have traces running through them to avoid shorts on a soldered in module!
