# Fritzing sketch 1_2_4 (saved by Fritzing 1.0.3b)
breadboards: 1

parts:
  A1 = Arduino UNO R4 WiFi
  S1 = Pushbutton [package="[THT]"]

nets:
  N1: A1.Pin_36, S1.Pin_1, S1.Pin_2
  N2: A1.Pin_48, S1.Pin_3, S1.Pin_4

custom parts:
  Arduino UNO R4 WiFi: The Arduino UNO R4 WiFi merges the RA4M1 microprocessor from Renesas with the ESP32-S3 from Espressif, creating an all-in-one tool for makers with enhanced processing power and a diverse array of new peripherals.
