# Fritzing sketch 3 (saved by Fritzing 1.0.3b)
breadboards: 1

parts:
  A2 = Arduino UNO R4 WiFi
  LED1 = LED - 5mm [color="Red (633nm)" current=0.030A package="5 mm [THT]"]
  R1 = Resistor [tolerance=±5% power=0.25W resistance=10k package=THT]
  LED2 = LED - 5mm [color="Yellow (595nm)" current=0.030A package="5 mm [THT]"]
  R3 = Resistor [tolerance=±5% power=0.25W resistance=10k package=THT]

nets:
  N1: A2.Pin_43, LED1.anode
  N2: A2.Pin_44, LED2.anode
  N3: A2.Pin_48, R1.Pin_0, R3.Pin_0
  N4: LED1.cathode, R1.Pin_1
  N5: LED2.cathode, R3.Pin_1

custom parts:
  Arduino UNO R4 WiFi: The Arduino UNO R4 WiFi merges the RA4M1 microprocessor from Renesas with the ESP32-S3 from Espressif, creating an all-in-one tool for makers with enhanced processing power and a diverse array of new peripherals.
