# Fritzing sketch 5_6 (saved by Fritzing 1.0.3b)
breadboards: 1

parts:
  A1 = Arduino UNO R4 WiFi
  S1 = Pushbutton [package="[THT]"]
  LED2 = LED - 5mm [color="Red (633nm)" current=0.030A package="5 mm [THT]"]
  R2 = Resistor [tolerance=±5% power=0.25W resistance=10k package=THT]

nets:
  N1: A1.Pin_36, S1.Pin_1, S1.Pin_2
  N2: A1.Pin_42, LED2.anode
  N3: A1.Pin_48, S1.Pin_3, S1.Pin_4, R2.Pin_0
  N4: LED2.cathode, R2.Pin_1

custom parts:
  Arduino UNO R4 WiFi: The Arduino UNO R4 WiFi merges the RA4M1 microprocessor from Renesas with the ESP32-S3 from Espressif, creating an all-in-one tool for makers with enhanced processing power and a diverse array of new peripherals.
