# Fritzing sketch 7_8 (saved by Fritzing 1.0.3b)
breadboards: 1

parts:
  A1 = Arduino UNO R4 WiFi
  R2 = Resistor [tolerance=±5% power=0.25W resistance=10k package=THT]
  LED1 = RGB LED PL9823 F5 [package="5 mm [THT]"]

nets:
  N1: A1.Pin_8, A1.Pin_27, LED1.GND
  N2: A1.Pin_42, R2.Pin_0
  N3: A1.Pin_48, LED1.VDD
  N4: R2.Pin_1, LED1.DO

custom parts:
  Arduino UNO R4 WiFi: The Arduino UNO R4 WiFi merges the RA4M1 microprocessor from Renesas with the ESP32-S3 from Espressif, creating an all-in-one tool for makers with enhanced processing power and a diverse array of new peripherals.
  RGB LED PL9823 F5: A 5mm tri-color LED with red, green and blue inside. this led includes WS2811 controller.
