# Fritzing sketch 3btn-mouse (saved by Fritzing 1.0.3b)
breadboards: 1

parts:
  A1 = Arduino UNO R4 WiFi
  S1 = Pushbutton [package="[THT]"]
  S2 = Pushbutton [package="[THT]"]
  S3 = Pushbutton [package="[THT]"]

nets:
  N1: A1.Pin_36, S1.Pin_1, S1.Pin_2
  N2: A1.Pin_37, S2.Pin_1, S2.Pin_2
  N3: A1.Pin_38, S3.Pin_1, S3.Pin_2
  N4: A1.Pin_48, S1.Pin_3, S1.Pin_4, S2.Pin_3, S2.Pin_4, S3.Pin_3, S3.Pin_4

custom parts:
  Arduino UNO R4 WiFi: The Arduino UNO R4 WiFi merges the RA4M1 microprocessor from Renesas with the ESP32-S3 from Espressif, creating an all-in-one tool for makers with enhanced processing power and a diverse array of new peripherals.
