# Fritzing sketch 1008_3-4 (saved by Fritzing 1.0.3b)
breadboards: 1

parts:
  パーツ2 = Arduino Uno (Rev3) - ICSP
  LED2 = smd LED [color="Red (633nm)" package="0603 [SMD]"]
  R1 = Resistor [tolerance=±5% power=0.25W resistance=1k package=THT]
  S2 = Pushbutton [package="[THT]"]

nets:
  N1: パーツ2.D8, R1.Pin_1
  N2: パーツ2.GND, LED2.cathode, S2.Pin_1, S2.Pin_2
  N3: パーツ2.D7, S2.Pin_3, S2.Pin_4
  N4: LED2.anode, R1.Pin_0
