# Fritzing sketch 1008_1-2 (saved by Fritzing 1.0.3b)
breadboards: 1

parts:
  パーツ1 = Arduino Uno (Rev3) - ICSP
  LED1 = smd LED [color="Red (633nm)" package="0603 [SMD]"]
  R1 = Resistor [tolerance=±5% power=0.25W resistance=1k package=THT]
  S1 = Pushbutton [package="[THT]"]
  R2 = Resistor [tolerance=±5% power=0.25W resistance=10k package=THT]

nets:
  5V: パーツ1.5V, S1.Pin_1, S1.Pin_2
  N1: パーツ1.D8, R1.Pin_1
  GND: パーツ1.GND, LED1.cathode, R2.Pin_0
  N2: パーツ1.D7, S1.Pin_3, S1.Pin_4, R2.Pin_1
  N3: LED1.anode, R1.Pin_0
