# Fritzing sketch 1008_3-4 (saved by Fritzing 1.0.3b)
breadboards: 1

parts:
  パーツ2 = Arduino Uno (Rev3) - ICSP
  LED1 = smd LED [color="Red (633nm)" package="0603 [SMD]"]
  R1 = Resistor [tolerance=±5% power=0.25W resistance=1k package=THT]
  S1 = Pushbutton [package="[THT]"]

nets:
  N1: パーツ2.D8, R1.Pin_1
  GND: パーツ2.GND, LED1.cathode, S1.Pin_1, S1.Pin_2
  N2: パーツ2.D7, S1.Pin_3, S1.Pin_4
  N3: LED1.anode, R1.Pin_0
