# Fritzing sketch 1008_5 (saved by Fritzing 1.0.3b)
breadboards: 1

parts:
  パーツ3 = Arduino Uno (Rev3) - ICSP
  LED1 = smd LED [color="Red (633nm)" package="0603 [SMD]"]
  R2 = Resistor [tolerance=±5% power=0.25W resistance=1k package=THT]
  S3 = Pushbutton [package="[THT]"]
  LED2 = smd LED [color="Red (633nm)" package="0603 [SMD]"]
  R1 = Resistor [tolerance=±5% power=0.25W resistance=1k package=THT]

nets:
  GND: パーツ3.GND, LED1.cathode, S3.Pin_1, S3.Pin_2, LED2.cathode
  N1: パーツ3.D8, R2.Pin_1
  N2: パーツ3.D9_PWM, R1.Pin_1
  N3: パーツ3.D7, S3.Pin_3, S3.Pin_4
  N4: LED1.anode, R1.Pin_0
  N5: R2.Pin_0, LED2.anode
