# Fritzing sketch 1008_8 (saved by Fritzing 1.0.3b)
breadboards: 1

parts:
  パーツ2 = Arduino Uno (Rev3) - ICSP
  LED1 = smd LED [color="Red (633nm)" package="0603 [SMD]"]
  R2 = Resistor [tolerance=±5% power=0.25W resistance=10k package=THT]
  R1 = Resistor [tolerance=±5% power=0.25W resistance=1k package=THT]
  R3 = Photocell (LDR) [power=0.25W dark_resistance_@0.01lx=300kΩ light_resistance_@100lx=400Ω luminance=10lx package=THT]
  S1 = Pushbutton [package="[THT]"]

nets:
  N1: パーツ2.A0, R2.Pin_1, R3.pin_0
  N2: パーツ2.D8, R1.Pin_1
  GND: パーツ2.GND, LED1.cathode, R2.Pin_0, S1.Pin_1, S1.Pin_2
  N3: パーツ2.D7, S1.Pin_3, S1.Pin_4
  5V: パーツ2.5V, R3.pin_1
  N4: LED1.anode, R1.Pin_0
