# Fritzing sketch 1015_1-2 (saved by Fritzing 1.0.3b)
breadboards: 2

parts:
  R1 = Resistor [tolerance=±5% power=0.25W resistance=1k package=THT]
  LED1 = smd LED [color="Red (633nm)" package="0603 [SMD]"]
  S1 = Pushbutton [package="[THT]"]
  Raspberry_Pi_Pico_W = Raspberry Pi Pico W
  Arduino_UNO = Arduino Uno (Rev3) - ICSP
  R2 = Resistor [tolerance=±5% power=0.25W resistance=1k package=THT]
  LED2 = smd LED [color="Red (633nm)" package="0603 [SMD]"]
  S2 = Pushbutton [package="[THT]"]

nets:
  N1: R1.Pin_0, Raspberry_Pi_Pico_W.pin_20
  N2: R1.Pin_1, LED1.anode
  RPi GND: LED1.cathode, S1.Pin_1, S1.Pin_2, Raspberry_Pi_Pico_W.pin_3, Raspberry_Pi_Pico_W.pin_8, Raspberry_Pi_Pico_W.pin_13, Raspberry_Pi_Pico_W.pin_18, Raspberry_Pi_Pico_W.pin_23, Raspberry_Pi_Pico_W.pin_28, Raspberry_Pi_Pico_W.pin_33, Raspberry_Pi_Pico_W.pin_38
  N3: S1.Pin_3, S1.Pin_4, Raspberry_Pi_Pico_W.pin_21
  N4: Arduino_UNO.D9_PWM, R2.Pin_1
  Arduino GND: Arduino_UNO.GND, LED2.cathode, S2.Pin_1, S2.Pin_2
  N5: Arduino_UNO.D7, S2.Pin_3, S2.Pin_4
  N6: R2.Pin_0, LED2.anode

custom parts:
  Raspberry Pi Pico W: Raspberry Pi Pico W. Based around the RP2040 microcontroller the Pico W is a low cost microcontroller device bringing Raspberry Pi quality, cost, and easy of use to the microcontroller space. The areas marked KEEPOUT in pcb silkscreen should not have traces running through them to avoid shorts on a soldered in module!
