# Fritzing sketch 1015_3 (saved by Fritzing 1.0.3b)
breadboards: 2

parts:
  R1 = Resistor [tolerance=±5% power=0.25W resistance=1k package=THT]
  LED1 = smd LED [color="Red (633nm)" package="0603 [SMD]"]
  Raspberry_Pi_Pico_W = Raspberry Pi Pico W
  Arduino_UNO = Arduino Uno (Rev3) - ICSP
  R3 = Resistor [tolerance=±5% power=0.25W resistance=1k package=THT]
  LED2 = smd LED [color="Red (633nm)" package="0603 [SMD]"]
  R6 = Photocell (LDR) [power=0.25W dark_resistance_@0.01lx=300kΩ light_resistance_@100lx=400Ω luminance=10lx package=THT]
  R4 = Resistor [tolerance=±5% power=0.25W resistance=10k package=THT]
  R5 = Photocell (LDR) [power=0.25W dark_resistance_@0.01lx=300kΩ light_resistance_@100lx=400Ω luminance=10lx package=THT]
  R2 = Resistor [tolerance=±5% power=0.25W resistance=10k package=THT]

nets:
  N1: R1.Pin_0, Raspberry_Pi_Pico_W.pin_20
  N2: R1.Pin_1, LED1.anode
  RPi GND: LED1.cathode, Raspberry_Pi_Pico_W.pin_3, Raspberry_Pi_Pico_W.pin_8, Raspberry_Pi_Pico_W.pin_13, Raspberry_Pi_Pico_W.pin_18, Raspberry_Pi_Pico_W.pin_23, Raspberry_Pi_Pico_W.pin_28, Raspberry_Pi_Pico_W.pin_33, Raspberry_Pi_Pico_W.pin_38, R2.Pin_0
  N3: Raspberry_Pi_Pico_W.pin_31, R5.pin_1, R2.Pin_1
  N4: Raspberry_Pi_Pico_W.pin_36, R5.pin_0
  N5: Arduino_UNO.A0, R6.pin_0, R4.Pin_1
  N6: Arduino_UNO.5V, R6.pin_1
  N7: Arduino_UNO.D9_PWM, R3.Pin_1
  Arduino GND: Arduino_UNO.GND, LED2.cathode, R4.Pin_0
  N8: R3.Pin_0, LED2.anode

custom parts:
  Raspberry Pi Pico W: Raspberry Pi Pico W. Based around the RP2040 microcontroller the Pico W is a low cost microcontroller device bringing Raspberry Pi quality, cost, and easy of use to the microcontroller space. The areas marked KEEPOUT in pcb silkscreen should not have traces running through them to avoid shorts on a soldered in module!
