# Fritzing sketch 1105-1 (saved by Fritzing 1.0.3b)

parts:
  Arduino_Uno = Arduino Uno (Rev3) - ICSP
  SERVO1 = Tower Pro SG90 servo [part_number=101246]

nets:
  N1: Arduino_Uno.D9_PWM, SERVO1.Signal
  5V: Arduino_Uno.5V, SERVO1.+5V
  GND: Arduino_Uno.GND, SERVO1.GND

custom parts:
  Tower Pro SG90 servo: Original file by John De Cristofaro http://www.adafruit.com/products/1449 Adafruit Feedback Servo (Small) Edited by: e-radionica.com 28/9/2015
