# Fritzing sketch 20241001 (saved by Fritzing 1.0.3b)
breadboards: 1

parts:
  パーツ1 = Arduino Uno (Rev3) - ICSP
  LED1 = smd LED [color="Red (633nm)" package="0603 [SMD]"]
  R1 = Resistor [tolerance=±5% power=0.25W resistance=1k package=THT]

nets:
  N1: パーツ1.ICSP_MOSI, パーツ1.D11_PWM/MOSI, R1.Pin_1
  N2: パーツ1.GND, LED1.cathode
  N3: LED1.anode, R1.Pin_0
